# Fritzing sketch pcd (saved by Fritzing 0.9.3b)
circuit board: 6.6592cm x 5.0996cm
breadboards: 1

parts:
  U1 = ESP8266 WiFi Module [part_number=ESP8266]
  DHT1 = DHT11 Humitidy and Temperature Sensor
  R1 = Resistor [tolerance=±5% resistance=220 package=THT]
  U2 = Optocoupler [package=THT]
  U3 = Voltage Regulator -- 3.3 V -- LM1117
  Power_plug1 = Power plug
  U4 = Voltage Regulator - 5V [package="TO220 [THT]"]
  U5 = RELAY-2 [package=relay-g5v]
  R2 = Resistor [tolerance=±5% resistance=220 package=THT]
  J1 = Camdenboss CTB0158-3 [part_number=CTB0158-3 package=THT]
  J2 = Camdenboss CTB0158-2 [part_number=CTB0158-2 package=THT]
  R3 = Resistor [tolerance=±5% resistance=220 package=THT]

nets (from the pcb view):
  N1: U1.RXD, U2.Pin_4
  N2: U1.VCC, U2.Pin_5, U3.OUT, R3.Pin_0
  N3: U1.GPIO_0, DHT1.DATA, R3.Pin_1
  N4: U1.GPIO_2, R1.Pin_1
  GND: U1.GND, DHT1.GND, U2.Pin_2, U3.GND, Power_plug1.GND, U4.GND, U5.9
  N5: DHT1.VDD, U3.IN, U4.output_voltage
  N6: R1.Pin_0, U5.2
  N7: U2.Pin_1, R2.Pin_0
  N8: Power_plug1.VCC, U4.input_voltage, J2.pin2
  N9: U5.1, J1.pin1
  N10: U5.6, J1.pin2
  N11: U5.10, J1.pin3
  N12: R2.Pin_1, J2.pin1

custom parts:
  ESP8266 WiFi Module: Generic WiFi Module based on the ESP8266 with onboard PCB antenna and UART communications
  DHT11 Humitidy and Temperature Sensor: DHT11 Humidity and Temperature Sensor
  Voltage Regulator -- 3.3 V -- LM1117: LM1117-3.3 Voltage regulator, 3.3 V output. Note that the pinout order is not the same as LM7805 or LM7833.
